# Fritzing sketch home_auto (saved by Fritzing 0.9.4)
circuit board: 19.3468cm x 11.9341cm
breadboards: 1

parts:
  J4 = Camdenboss CTB0158-8 [part_number=CTB0158-8 package=THT]
  J5 = Camdenboss CTB0158-8 [part_number=CTB0158-8 package=THT]
  J8 = Camdenboss CTB0158-8 [part_number=CTB0158-8 package=THT]
  J3 = Camdenboss CTB0158-8 [part_number=CTB0158-8 package=THT]
  Q1 = Basic FET P-Channel [package="TO220 [THT]"]
  Q3 = Basic FET P-Channel [package="TO220 [THT]"]
  Q4 = Basic FET P-Channel [package="TO220 [THT]"]
  Q5 = Basic FET P-Channel [package="TO220 [THT]"]
  Q6 = Basic FET P-Channel [package="TO220 [THT]"]
  Q7 = Basic FET P-Channel [package="TO220 [THT]"]
  Arduino_Mega = Arduino Mega 2560 (Rev3)
  J10 = Camdenboss CTB0158-8 [part_number=CTB0158-8 package=THT]
  Q9 = Basic FET P-Channel [package="TO220 [THT]"]
  Q15 = Basic FET P-Channel [package="TO220 [THT]"]
  Q10 = Basic FET P-Channel [package="TO220 [THT]"]
  Q13 = Basic FET P-Channel [package="TO220 [THT]"]
  Q11 = Basic FET P-Channel [package="TO220 [THT]"]
  Q14 = Basic FET P-Channel [package="TO220 [THT]"]
  Q16 = Basic FET P-Channel [package="TO220 [THT]"]
  J11 = Camdenboss CTB0158-8 [part_number=CTB0158-8 package=THT]
  J6 = Camdenboss CTB0158-8 [part_number=CTB0158-8 package=THT]
  Q12 = Basic FET P-Channel [package="TO220 [THT]"]
  Pad3 = Pad [width=8.425944997050134 height=7.380860373647994 connect=center]
  Pad4 = Pad [width=8.425944997050134 height=7.380860373647994 connect=center]
  R25 = Resistor [tolerance=±5% resistance=220 package=THT]
  R24 = Resistor [tolerance=±5% resistance=220 package=THT]
  R23 = Resistor [tolerance=±5% resistance=220 package=THT]
  R26 = Resistor [tolerance=±5% resistance=220 package=THT]
  R55 = Resistor [tolerance=±5% resistance=220 package=THT]
  R56 = Resistor [tolerance=±5% resistance=220 package=THT]
  R33 = Resistor [tolerance=±5% resistance=220 package=THT]
  R54 = Resistor [tolerance=±5% resistance=220 package=THT]
  R22 = Resistor [tolerance=±5% resistance=220 package=THT]
  R20 = Resistor [tolerance=±5% resistance=220 package=THT]
  R21 = Resistor [tolerance=±5% resistance=220 package=THT]
  R19 = Resistor [tolerance=±5% resistance=220 package=THT]
  R15 = Resistor [tolerance=±5% resistance=220 package=THT]
  R18 = Resistor [tolerance=±5% resistance=220 package=THT]
  R16 = Resistor [tolerance=±5% resistance=220 package=THT]
  R17 = Resistor [tolerance=±5% resistance=220 package=THT]
  J12 = Camdenboss CTB0158-8 [part_number=CTB0158-8 package=THT]
  R63 = Resistor [tolerance=±5% resistance=220 package=THT]
  R64 = Resistor [tolerance=±5% resistance=220 package=THT]
  R59 = Resistor [tolerance=±5% resistance=220 package=THT]
  R58 = Resistor [tolerance=±5% resistance=220 package=THT]
  R62 = Resistor [tolerance=±5% resistance=220 package=THT]
  R61 = Resistor [tolerance=±5% resistance=220 package=THT]
  R60 = Resistor [tolerance=±5% resistance=220 package=THT]
  R57 = Resistor [tolerance=±5% resistance=220 package=THT]
  J14 = Camdenboss CTB0158-8 [part_number=CTB0158-8 package=THT]
  R35 = Resistor [tolerance=±5% resistance=220 package=THT]
  R53 = Resistor [tolerance=±5% resistance=220 package=THT]
  R36 = Resistor [tolerance=±5% resistance=220 package=THT]
  R34 = Resistor [tolerance=±5% resistance=220 package=THT]
  R11 = Resistor [tolerance=±5% resistance=220 package=THT]
  R12 = Resistor [tolerance=±5% resistance=220 package=THT]
  R09 = Resistor [tolerance=±5% resistance=220 package=THT]
  R10 = Resistor [tolerance=±5% resistance=220 package=THT]
  R04 = Resistor [tolerance=±5% resistance=220 package=THT]
  R05 = Resistor [tolerance=±5% resistance=220 package=THT]
  R06 = Resistor [tolerance=±5% resistance=220 package=THT]
  R07 = Resistor [tolerance=±5% resistance=220 package=THT]
  R08 = Resistor [tolerance=±5% resistance=220 package=THT]
  R03 = Resistor [tolerance=±5% resistance=220 package=THT]
  R02 = Resistor [tolerance=±5% resistance=220 package=THT]
  R01 = Resistor [tolerance=±5% resistance=220 package=THT]
  R27 = Resistor [tolerance=±5% resistance=220 package=THT]
  R28 = Resistor [tolerance=±5% resistance=220 package=THT]
  R29 = Resistor [tolerance=±5% resistance=220 package=THT]
  R32 = Resistor [tolerance=±5% resistance=220 package=THT]
  R31 = Resistor [tolerance=±5% resistance=220 package=THT]
  R30 = Resistor [tolerance=±5% resistance=220 package=THT]
  Pad5 = Pad [width=8.425944997050134 height=7.380860373647994 connect=center]
  Pad6 = Pad [width=8.425944997050134 height=7.380860373647994 connect=center]
  Pad7 = Pad [width=8.425944997050134 height=7.380860373647994 connect=center]
  Pad8 = Pad [width=8.425944997050134 height=7.380860373647994 connect=center]
  Pad9 = Pad [width=8.425944997050134 height=7.380860373647994 connect=center]
  Pad10 = Pad [width=8.425944997050134 height=7.380860373647994 connect=center]
  R14 = Resistor [tolerance=±5% resistance=220 package=THT]
  R13 = Resistor [tolerance=±5% resistance=220 package=THT]
  S1 = SWITCH-MOMENTARY-2 [package=tactile-pth-12mm]
  Q2 = Basic FET P-Channel [package="TO220 [THT]"]
  R49 = Resistor [tolerance=±5% resistance=220 package=THT]
  R42 = Resistor [tolerance=±5% resistance=220 package=THT]
  R37 = Resistor [tolerance=±5% resistance=220 package=THT]
  R39 = Resistor [tolerance=±5% resistance=220 package=THT]
  R41 = Resistor [tolerance=±5% resistance=220 package=THT]
  R50 = Resistor [tolerance=±5% resistance=220 package=THT]
  R43 = Resistor [tolerance=±5% resistance=220 package=THT]
  R38 = Resistor [tolerance=±5% resistance=220 package=THT]
  R52 = Resistor [tolerance=±5% resistance=220 package=THT]
  R51 = Resistor [tolerance=±5% resistance=220 package=THT]
  R40 = Resistor [tolerance=±5% resistance=220 package=THT]
  R44 = Resistor [tolerance=±5% resistance=220 package=THT]
  R45 = Resistor [tolerance=±5% resistance=220 package=THT]
  R46 = Resistor [tolerance=±5% resistance=220 package=THT]
  R47 = Resistor [tolerance=±5% resistance=220 package=THT]
  R48 = Resistor [tolerance=±5% resistance=220 package=THT]
  W5100 = header for W5100 board (upside down) [package=avr_icsp]
  D1 = Rectifier Diode [part_number=1N4001 package="300 mil [THT]"]
  D2 = Rectifier Diode [part_number=1N4001 package="300 mil [THT]"]
  D3 = Rectifier Diode [part_number=1N4001 package="300 mil [THT]"]
  D4 = Rectifier Diode [part_number=1N4001 package="300 mil [THT]"]
  D5 = Rectifier Diode [part_number=1N4001 package="300 mil [THT]"]
  D6 = Rectifier Diode [part_number=1N4001 package="300 mil [THT]"]
  D7 = Rectifier Diode [part_number=1N4001 package="300 mil [THT]"]
  D8 = Rectifier Diode [part_number=1N4001 package="300 mil [THT]"]
  D9 = Rectifier Diode [part_number=1N4001 package="300 mil [THT]"]
  D10 = Rectifier Diode [part_number=1N4001 package="300 mil [THT]"]
  D11 = Rectifier Diode [part_number=1N4001 package="300 mil [THT]"]
  D12 = Rectifier Diode [part_number=1N4001 package="300 mil [THT]"]
  D13 = Rectifier Diode [part_number=1N4001 package="300 mil [THT]"]
  D14 = Rectifier Diode [part_number=1N4001 package="300 mil [THT]"]
  D15 = Rectifier Diode [part_number=1N4001 package="300 mil [THT]"]
  D0 = Rectifier Diode [part_number=1N4001 package="300 mil [THT]"]
  Q8 = Basic FET P-Channel [package="TO220 [THT]"]
  C1 = Electrolytic Capacitor [capacitance=1µF package="100 mil [THT, electrolytic]"]  # not connected
  C2 = Capacitor Polarized [package=panasonic_c]  # not connected
  C3 = Electrolytic Capacitor [capacitance=100µF package="200 mil [THT, electrolytic]"]
  C4 = Electrolytic Capacitor [capacitance=100µF package="200 mil [THT, electrolytic]"]

nets:
  N1: J4.pin1, Arduino_Mega.D26, R15.Pin_0
  N2: J4.pin2, Arduino_Mega.D27, R29.Pin_1
  N3: J4.pin3, Arduino_Mega.D28, R16.Pin_0
  N4: J4.pin4, Arduino_Mega.D29, R30.Pin_1
  N5: J4.pin5, Arduino_Mega.D30, R17.Pin_0
  N6: J4.pin6, Arduino_Mega.D31, R31.Pin_1
  N7: J4.pin7, Arduino_Mega.D32, R18.Pin_0
  N8: J4.pin8, Arduino_Mega.D33, R32.Pin_1
  N9: J5.pin1, Arduino_Mega.D2_PWM, R10.Pin_1
  N10: J5.pin2, Arduino_Mega.D3_PWM, R09.Pin_1
  N11: J5.pin3, Arduino_Mega.D16_PWM/TX2, R11.Pin_1
  N12: J5.pin4, Arduino_Mega.D17_PWM/RX2, R12.Pin_1
  N13: J5.pin5, Arduino_Mega.D22, R13.Pin_0
  N14: J5.pin6, Arduino_Mega.D23, R27.Pin_1
  N15: J5.pin7, Arduino_Mega.D24, R14.Pin_0
  N16: J5.pin8, Arduino_Mega.D25, R28.Pin_1
  N17: J8.pin1, Q1.drain, D0.anode
  N18: J8.pin2, Q2.drain, D1.anode
  N19: J8.pin3, Q3.drain, D2.anode
  N20: J8.pin4, Q4.drain, D3.anode
  N21: J8.pin5, Q5.drain, D4.anode
  N22: J8.pin6, Q6.drain, D5.anode
  N23: J8.pin7, Q7.drain, D6.anode
  N24: J8.pin8, D7.anode, Q8.drain
  5V: J3.pin1, J3.pin2, J3.pin3, J3.pin4, Arduino_Mega.5V, J6.pin5, J6.pin6, J6.pin7, J6.pin8, Pad4.pad, R15.Pin_1, R18.Pin_1, R16.Pin_1, R17.Pin_1, R63.Pin_1, R64.Pin_1, R59.Pin_1, R58.Pin_1, R62.Pin_1, R61.Pin_1, R60.Pin_1, R57.Pin_1, R11.Pin_0, R12.Pin_0, R09.Pin_0, R10.Pin_0, R04.Pin_0, R05.Pin_0, R06.Pin_0, R07.Pin_0, R08.Pin_0, R03.Pin_0, R02.Pin_0, R01.Pin_0, R27.Pin_0, R28.Pin_0, R29.Pin_0, R32.Pin_0, R31.Pin_0, R30.Pin_0, Pad10.pad, R14.Pin_1, R13.Pin_1, W5100.5v, C3.-
  GND: J3.pin5, J3.pin6, J3.pin7, J3.pin8, Q1.source, Q3.source, Q4.source, Q5.source, Q6.source, Q7.source, Arduino_Mega.GND, Q9.source, Q15.source, Q10.source, Q13.source, Q11.source, Q14.source, Q16.source, J11.pin5, J11.pin6, J11.pin7, J11.pin8, J6.pin1, J6.pin2, J6.pin3, J6.pin4, Q12.source, Pad3.pad, R25.Pin_1, R24.Pin_1, R23.Pin_1, R26.Pin_1, R55.Pin_1, R56.Pin_1, R33.Pin_0, R54.Pin_1, R22.Pin_1, R20.Pin_1, R21.Pin_1, R19.Pin_1, R35.Pin_0, R53.Pin_0, R36.Pin_0, R34.Pin_0, Pad5.pad, Pad8.pad, Pad9.pad, S1.1, Q2.source, W5100.gnd, Q8.source, C3.+, C4.+
  N25: Q1.gate, R41.Pin_1
  N26: Q3.gate, R42.Pin_1
  N27: Q4.gate, R38.Pin_1
  N28: Q5.gate, R43.Pin_1
  N29: Q6.gate, R39.Pin_1
  N30: Q7.gate, R44.Pin_1
  N31: Arduino_Mega.A0, J12.pin8, R57.Pin_0
  N32: Arduino_Mega.A1, J12.pin7, R58.Pin_0
  N33: Arduino_Mega.A2, J12.pin6, R59.Pin_0
  N34: Arduino_Mega.A3, J12.pin5, R60.Pin_0
  N35: Arduino_Mega.A4, J12.pin4, R61.Pin_0
  N36: Arduino_Mega.A5, J12.pin3, R62.Pin_0
  N37: Arduino_Mega.A6, J12.pin2, R63.Pin_0
  N38: Arduino_Mega.A7, J12.pin1, R64.Pin_0
  N39: Arduino_Mega.D12_PWM, W5100.rst
  N40: Arduino_Mega.D11_PWM, J14.pin1, R02.Pin_1
  N41: Arduino_Mega.D10_PWM, J14.pin2, R03.Pin_1
  N42: Arduino_Mega.D9_PWM, J14.pin3, R04.Pin_1
  N43: Arduino_Mega.D8_PWM, J14.pin4, R05.Pin_1
  N44: Arduino_Mega.RESET, S1.2
  N45: Arduino_Mega.D4_PWM, J14.pin8, R01.Pin_1
  N46: Arduino_Mega.D5_PWM, J14.pin7, R08.Pin_1
  N47: Arduino_Mega.D6_PWM, J14.pin6, R07.Pin_1
  N48: Arduino_Mega.D7_PWM, J14.pin5, R06.Pin_1
  N49: Arduino_Mega.D34, R19.Pin_0, R41.Pin_0
  N50: Arduino_Mega.D35, R33.Pin_1, R37.Pin_0
  N51: Arduino_Mega.D36, R20.Pin_0, R42.Pin_0
  N52: Arduino_Mega.D37, R34.Pin_1, R38.Pin_0
  N53: Arduino_Mega.D38, R21.Pin_0, R43.Pin_0
  N54: Arduino_Mega.D39, R35.Pin_1, R39.Pin_0
  N55: Arduino_Mega.D40, R22.Pin_0, R44.Pin_0
  N56: Arduino_Mega.D41, R36.Pin_1, R40.Pin_0
  N57: Arduino_Mega.D42, R23.Pin_0, R49.Pin_0
  N58: Arduino_Mega.D43, R53.Pin_1, R45.Pin_0
  N59: Arduino_Mega.D44, R24.Pin_0, R50.Pin_0
  N60: Arduino_Mega.D45, R54.Pin_0, R46.Pin_0
  N61: Arduino_Mega.D46, R25.Pin_0, R51.Pin_0
  N62: Arduino_Mega.D47, R55.Pin_0, R47.Pin_0
  N63: Arduino_Mega.D48, R26.Pin_0, R52.Pin_0
  N64: Arduino_Mega.D49, R56.Pin_0, R48.Pin_0
  N65: Arduino_Mega.D50, W5100.mi
  N66: Arduino_Mega.D51, W5100.mo
  N67: Arduino_Mega.D52, W5100.sok
  N68: Arduino_Mega.D53, W5100.ss
  N69: J10.pin1, Q9.drain, D8.anode
  N70: J10.pin2, Q10.drain, D9.anode
  N71: J10.pin3, Q11.drain, D10.anode
  N72: J10.pin4, Q12.drain, D11.anode
  N73: J10.pin5, Q13.drain, D12.anode
  N74: J10.pin6, Q14.drain, D13.anode
  N75: J10.pin7, Q15.drain, D14.anode
  N76: J10.pin8, Q16.drain, D15.anode
  N77: Q9.gate, R49.Pin_1
  N78: Q15.gate, R52.Pin_1
  N79: Q10.gate, R45.Pin_1
  N80: Q13.gate, R51.Pin_1
  N81: Q11.gate, R50.Pin_1
  N82: Q14.gate, R47.Pin_1
  N83: Q16.gate, R48.Pin_1
  N84: J11.pin1, J11.pin2, J11.pin3, J11.pin4, Pad6.pad, Pad7.pad, D1.cathode, D2.cathode, D3.cathode, D4.cathode, D5.cathode, D6.cathode, D7.cathode, D8.cathode, D9.cathode, D10.cathode, D11.cathode, D12.cathode, D13.cathode, D14.cathode, D15.cathode, D0.cathode, C4.-
  N85: Q12.gate, R46.Pin_1
  N86: Q2.gate, R37.Pin_1
  N87: R40.Pin_1, Q8.gate

notes:
  4xGND|4x5V
  4x24V|4xGND
  2020 by AK
  Schaltplan:
  - Eingänge mit Pullup Widerstand
  - FETs mit Pulldown Widerstand
  - FET: IRF520
  - Connectoren: 5,1mm Pitch, schraub & steck
  - DC -DC Wandler extern über Lötpads & Schraubbolzen
  - Pins 4, 10, 50 - 53 bleiben frei wegen Ethernet-Shield
  - A8-15 werden nicht benötigt.
  - Stützkondensator notwendig?
  - FET Schaltung okay?
  Routing:
  - DRC ist fehelrfrei (fritzing default)
  - die "dünnen" traces hab ich maximal dünn machen müssen (8 mil) damit es keinen DRC fehler gibt.
  - gefühlt könnte man sie auch 12 mil machen?
  D25-22 D17/16/3/2
  D4-11
  D33-26
  D34-49(FETs)
  A7-15
  D53 D12
  5V  GND
  D51 D52
  GND D50
  GND / 24V
  => Geht auf externen DC DC Wandler
  => 5V Schiene
