# Fritzing sketch home_auto_v011 (saved by Fritzing 0.9.4)
circuit board: 19.3468cm x 11.4617cm
breadboards: 1

parts:
  J4 = Camdenboss CTB0158-8 [part_number=CTB0158-8 package=THT]
  J5 = Camdenboss CTB0158-8 [part_number=CTB0158-8 package=THT]
  J8 = Camdenboss CTB0158-8 [part_number=CTB0158-8 package=THT]
  J3 = Camdenboss CTB0158-8 [part_number=CTB0158-8 package=THT]
  Q1 = Basic FET P-Channel [package="TO220 [THT]"]
  Q3 = Basic FET P-Channel [package="TO220 [THT]"]
  Q4 = Basic FET P-Channel [package="TO220 [THT]"]
  Q5 = Basic FET P-Channel [package="TO220 [THT]"]
  Q6 = Basic FET P-Channel [package="TO220 [THT]"]
  Q7 = Basic FET P-Channel [package="TO220 [THT]"]
  Q8 = Basic FET P-Channel [package="TO220 [THT]"]
  Arduino_Mega = Arduino Mega 2560 (Rev3)
  J10 = Camdenboss CTB0158-8 [part_number=CTB0158-8 package=THT]
  Q9 = Basic FET P-Channel [package="TO220 [THT]"]
  Q15 = Basic FET P-Channel [package="TO220 [THT]"]
  Q10 = Basic FET P-Channel [package="TO220 [THT]"]
  Q13 = Basic FET P-Channel [package="TO220 [THT]"]
  Q11 = Basic FET P-Channel [package="TO220 [THT]"]
  Q14 = Basic FET P-Channel [package="TO220 [THT]"]
  Q16 = Basic FET P-Channel [package="TO220 [THT]"]
  J11 = Camdenboss CTB0158-8 [part_number=CTB0158-8 package=THT]
  J6 = Camdenboss CTB0158-8 [part_number=CTB0158-8 package=THT]
  Q12 = Basic FET P-Channel [package="TO220 [THT]"]
  Pad3 = Pad [width=8.425944997050134 height=7.380860373647994 connect=center]
  Pad4 = Pad [width=8.425944997050134 height=7.380860373647994 connect=center]
  R25 = Resistor [tolerance=±5% resistance=220 package=THT]
  R24 = Resistor [tolerance=±5% resistance=220 package=THT]
  R23 = Resistor [tolerance=±5% resistance=220 package=THT]
  R26 = Resistor [tolerance=±5% resistance=220 package=THT]
  R70 = Resistor [tolerance=±5% resistance=220 package=THT]
  R71 = Resistor [tolerance=±5% resistance=220 package=THT]
  R72 = Resistor [tolerance=±5% resistance=220 package=THT]
  R73 = Resistor [tolerance=±5% resistance=220 package=THT]
  R22 = Resistor [tolerance=±5% resistance=220 package=THT]
  R20 = Resistor [tolerance=±5% resistance=220 package=THT]
  R21 = Resistor [tolerance=±5% resistance=220 package=THT]
  R19 = Resistor [tolerance=±5% resistance=220 package=THT]
  R15 = Resistor [tolerance=±5% resistance=220 package=THT]
  R18 = Resistor [tolerance=±5% resistance=220 package=THT]
  R16 = Resistor [tolerance=±5% resistance=220 package=THT]
  R17 = Resistor [tolerance=±5% resistance=220 package=THT]
  J12 = Camdenboss CTB0158-8 [part_number=CTB0158-8 package=THT]
  R83 = Resistor [tolerance=±5% resistance=220 package=THT]
  R84 = Resistor [tolerance=±5% resistance=220 package=THT]
  R85 = Resistor [tolerance=±5% resistance=220 package=THT]
  R86 = Resistor [tolerance=±5% resistance=220 package=THT]
  R87 = Resistor [tolerance=±5% resistance=220 package=THT]
  R88 = Resistor [tolerance=±5% resistance=220 package=THT]
  R89 = Resistor [tolerance=±5% resistance=220 package=THT]
  R90 = Resistor [tolerance=±5% resistance=220 package=THT]
  J14 = Camdenboss CTB0158-8 [part_number=CTB0158-8 package=THT]
  R91 = Resistor [tolerance=±5% resistance=220 package=THT]
  R92 = Resistor [tolerance=±5% resistance=220 package=THT]
  R93 = Resistor [tolerance=±5% resistance=220 package=THT]
  R94 = Resistor [tolerance=±5% resistance=220 package=THT]
  R11 = Resistor [tolerance=±5% resistance=220 package=THT]
  R12 = Resistor [tolerance=±5% resistance=220 package=THT]
  R09 = Resistor [tolerance=±5% resistance=220 package=THT]
  R10 = Resistor [tolerance=±5% resistance=220 package=THT]
  R04 = Resistor [tolerance=±5% resistance=220 package=THT]
  R05 = Resistor [tolerance=±5% resistance=220 package=THT]
  R06 = Resistor [tolerance=±5% resistance=220 package=THT]
  R07 = Resistor [tolerance=±5% resistance=220 package=THT]
  R08 = Resistor [tolerance=±5% resistance=220 package=THT]
  R03 = Resistor [tolerance=±5% resistance=220 package=THT]
  R02 = Resistor [tolerance=±5% resistance=220 package=THT]
  R01 = Resistor [tolerance=±5% resistance=220 package=THT]
  R107 = Resistor [tolerance=±5% resistance=220 package=THT]
  R108 = Resistor [tolerance=±5% resistance=220 package=THT]
  R109 = Resistor [tolerance=±5% resistance=220 package=THT]
  R110 = Resistor [tolerance=±5% resistance=220 package=THT]
  R111 = Resistor [tolerance=±5% resistance=220 package=THT]
  R112 = Resistor [tolerance=±5% resistance=220 package=THT]
  Pad5 = Pad [width=8.425944997050134 height=7.380860373647994 connect=center]
  Pad6 = Pad [width=8.425944997050134 height=7.380860373647994 connect=center]
  Pad7 = Pad [width=8.425944997050134 height=7.380860373647994 connect=center]
  Pad8 = Pad [width=8.425944997050134 height=7.380860373647994 connect=center]
  Pad9 = Pad [width=8.425944997050134 height=7.380860373647994 connect=center]
  Pad10 = Pad [width=8.425944997050134 height=7.380860373647994 connect=center]
  R14 = Resistor [tolerance=±5% resistance=220 package=THT]
  R13 = Resistor [tolerance=±5% resistance=220 package=THT]
  ICSP = AVR ISP 6 Pin [package=2x3-ns]  # not connected
  S1 = SWITCH-MOMENTARY-2 [package=tactile-pth-12mm]
  Q2 = Basic FET P-Channel [package="TO220 [THT]"]

nets:
  N1: J4.pin1, Arduino_Mega.D26, R15.Pin_0
  N2: J4.pin2, Arduino_Mega.D28, R16.Pin_0
  N3: J4.pin3, Arduino_Mega.D30, R17.Pin_0
  N4: J4.pin4, Arduino_Mega.D32, R18.Pin_0
  N5: J4.pin5, Arduino_Mega.D27, R109.Pin_1
  N6: J4.pin6, Arduino_Mega.D29, R112.Pin_1
  N7: J4.pin7, Arduino_Mega.D31, R111.Pin_1
  N8: J4.pin8, Arduino_Mega.D33, R110.Pin_1
  N9: J5.pin1, Arduino_Mega.D3_PWM, R09.Pin_1
  N10: J5.pin2, Arduino_Mega.D2_PWM, R10.Pin_1
  N11: J5.pin3, Arduino_Mega.D16_PWM/TX2, R11.Pin_1
  N12: J5.pin4, Arduino_Mega.D17_PWM/RX2, R12.Pin_1
  N13: J5.pin5, Arduino_Mega.D22, R13.Pin_0
  N14: J5.pin6, Arduino_Mega.D24, R14.Pin_0
  N15: J5.pin7, Arduino_Mega.D23, R107.Pin_1
  N16: J5.pin8, Arduino_Mega.D25, R108.Pin_1
  N17: J8.pin1, Q1.drain
  N18: J8.pin2, Q2.drain
  N19: J8.pin3, Q3.drain
  N20: J8.pin4, Q4.drain
  N21: J8.pin5, Q5.drain
  N22: J8.pin6, Q6.drain
  N23: J8.pin7, Q7.drain
  N24: J8.pin8, Q8.drain
  N25: J3.pin1, J3.pin2, J3.pin3, J3.pin4, Arduino_Mega.5V, J6.pin5, J6.pin6, J6.pin7, J6.pin8, Pad4.pad, R15.Pin_1, R18.Pin_1, R16.Pin_1, R17.Pin_1, R83.Pin_1, R84.Pin_1, R85.Pin_1, R86.Pin_1, R87.Pin_1, R88.Pin_1, R89.Pin_1, R90.Pin_1, R11.Pin_0, R12.Pin_0, R09.Pin_0, R10.Pin_0, R04.Pin_0, R05.Pin_0, R06.Pin_0, R07.Pin_0, R08.Pin_0, R03.Pin_0, R02.Pin_0, R01.Pin_0, R107.Pin_0, R108.Pin_0, R109.Pin_0, R110.Pin_0, R111.Pin_0, R112.Pin_0, Pad10.pad, R14.Pin_1, R13.Pin_1
  N26: J3.pin5, J3.pin6, J3.pin7, J3.pin8, Q1.source, Q3.source, Q4.source, Q5.source, Q6.source, Q7.source, Q8.source, Arduino_Mega.GND, Q9.source, Q15.source, Q10.source, Q13.source, Q11.source, Q14.source, Q16.source, J11.pin5, J11.pin6, J11.pin7, J11.pin8, J6.pin1, J6.pin2, J6.pin3, J6.pin4, Q12.source, Pad3.pad, R25.Pin_1, R24.Pin_1, R23.Pin_1, R26.Pin_1, R70.Pin_1, R71.Pin_1, R72.Pin_0, R73.Pin_1, R22.Pin_1, R20.Pin_1, R21.Pin_1, R19.Pin_1, R91.Pin_0, R92.Pin_0, R93.Pin_0, R94.Pin_0, Pad5.pad, Pad8.pad, Pad9.pad, S1.1, Q2.source
  N27: Q1.gate, Arduino_Mega.D35, R72.Pin_1
  N28: Q3.gate, Arduino_Mega.D39, R91.Pin_1
  N29: Q4.gate, Arduino_Mega.D41, R93.Pin_1
  N30: Q5.gate, Arduino_Mega.D34, R19.Pin_0
  N31: Q6.gate, Arduino_Mega.D36, R20.Pin_0
  N32: Q7.gate, Arduino_Mega.D38, R21.Pin_0
  N33: Q8.gate, Arduino_Mega.D40, R22.Pin_0
  N34: Arduino_Mega.A0, J12.pin8, R90.Pin_0
  N35: Arduino_Mega.A1, J12.pin7, R86.Pin_0
  N36: Arduino_Mega.A2, J12.pin6, R85.Pin_0
  N37: Arduino_Mega.A3, J12.pin5, R89.Pin_0
  N38: Arduino_Mega.A4, J12.pin4, R88.Pin_0
  N39: Arduino_Mega.A5, J12.pin3, R87.Pin_0
  N40: Arduino_Mega.A6, J12.pin2, R83.Pin_0
  N41: Arduino_Mega.A7, J12.pin1, R84.Pin_0
  N42: Arduino_Mega.D13_PWM, J14.pin1, R01.Pin_1
  N43: Arduino_Mega.D12_PWM, J14.pin2, R02.Pin_1
  N44: Arduino_Mega.D11_PWM, J14.pin3, R03.Pin_1
  N45: Arduino_Mega.D9_PWM, J14.pin4, R04.Pin_1
  N46: Arduino_Mega.D8_PWM, J14.pin5, R05.Pin_1
  N47: Arduino_Mega.RESET, S1.2
  N48: Arduino_Mega.D5_PWM, J14.pin8, R08.Pin_1
  N49: Arduino_Mega.D6_PWM, J14.pin7, R07.Pin_1
  N50: Arduino_Mega.D7_PWM, J14.pin6, R06.Pin_1
  N51: Arduino_Mega.D37, R94.Pin_1, Q2.gate
  N52: Arduino_Mega.D42, Q9.gate, R23.Pin_0
  N53: Arduino_Mega.D43, Q13.gate, R92.Pin_1
  N54: Arduino_Mega.D44, Q10.gate, R24.Pin_0
  N55: Arduino_Mega.D45, Q14.gate, R73.Pin_0
  N56: Arduino_Mega.D46, Q11.gate, R25.Pin_0
  N57: Arduino_Mega.D47, Q15.gate, R70.Pin_0
  N58: Arduino_Mega.D48, Q12.gate, R26.Pin_0
  N59: Arduino_Mega.D49, Q16.gate, R71.Pin_0
  N60: J10.pin1, Q9.drain
  N61: J10.pin2, Q10.drain
  N62: J10.pin3, Q11.drain
  N63: J10.pin4, Q12.drain
  N64: J10.pin5, Q13.drain
  N65: J10.pin6, Q14.drain
  N66: J10.pin7, Q15.drain
  N67: J10.pin8, Q16.drain
  N68: J11.pin1, J11.pin2, J11.pin3, J11.pin4, Pad6.pad, Pad7.pad

notes:
  4xGND|4x5V
  4xV+|4xGND
  2020 by AK
  Schaltplan:
  - Eingänge mit Pullup Widerstand
  - FETs mit Pulldown Widerstand
  - FET: IRF520
  - Connectoren: 5,1mm Pitch, schraub & steck
  - DC -DC Wandler extern über Lötpads & Schraubbolzen
  - Pins 4, 10, 50 - 53 bleiben frei wegen Ethernet-Shield
  - A8-15 werden nicht benötigt.
  - Stützkondensator notwendig?
  - FET Schaltung okay?
  Routing:
  - DRC ist fehelrfrei (fritzing default)
  - die "dünnen" traces hab ich maximal dünn machen müssen (8 mil) damit es keinen DRC fehler gibt.
  - gefühlt könnte man sie auch 12 mil machen?
